// Digital circuit Single-cycle-RISCV.dig as structural Verilog
module Single_cycle_RISCV (
  input  clk,
  input  in_2
);

  wire aluSrcB, and_1_out, branch, btype, csr, dipswitch_1_out, dipswitch_2_out, dipswitch_3_out,
       dipswitch_4_out, dipswitch_5_out, dipswitch_6_out, dipswitch_7_out, dipswitch_8_out, exception,
       interrupt, jalr, keyboard_1_av, load, pcSrc, store, trap, u_disp_vwe, u_term_key_en, u_term_term_en,
       uret, wreg;
  wire [1:0] wregSrc;
  wire [2:0] funct3;
  wire [3:0] ALU_op;
  wire [4:0] rd, rs1, rs2;
  wire [7:0] u_disp_vdata, u_led_led, u_term_term_data;
  wire [11:0] csr_addr;
  wire [14:0] u_disp_vaddr;
  wire [15:0] keyboard_1_d;
  wire [19:0] u_code_data;
  wire [31:0] c, cause, csrReadData, dout, epc, Imm, jal_jalr, memReadData, memWriteData, multiplexer_1_out,
       multiplexer_2_out, multiplexer_3_out, multiplexer_4_out, multiplexer_5_out, multiplexer_6_out, pc,
       pc_plus_4, r1, u_csr_op_c, u_even_fout, utvec;

  and and_1 (and_1_out, btype, branch);
  even #(.applicationType("IVERILOG"), .CodeFile("C:\\Users\\kevin\\Desktop\\Single-cycle-RISCV\\user\\src\\even.v")) u_even (
    .din(jal_jalr), .fout(u_even_fout));
  Multiplexer #(.Bits(32)) multiplexer_1 (.sel(and_1_out), .in_0(pc_plus_4), .in_1(jal_jalr), .out(multiplexer_1_out));
  Multiplexer #(.Bits(32)) multiplexer_2 (
    .sel(pcSrc), .in_0(multiplexer_1_out), .in_1(u_even_fout), .out(multiplexer_2_out));
  add_4 #(.applicationType("IVERILOG"), .CodeFile("C:\\Users\\kevin\\Desktop\\Single-cycle-RISCV\\user\\src\\add_4.v")) u_add_4 (
    .in_pc(pc), .out_pc(pc_plus_4));
  PC #(.applicationType("IVERILOG"), .CodeFile("C:\\Users\\kevin\\Desktop\\Single-cycle-RISCV\\user\\src\\PC.v")) u_PC (
    .clk(clk), .rstn(in_2), .next_pc(multiplexer_2_out), .trap(trap), .utvec(utvec), .uret(uret), .epc(epc),
    .pc(pc));
  code #(.applicationType("IVERILOG"), .CodeFile("C:\\Users\\kevin\\Desktop\\Single-cycle-RISCV\\user\\src\\code.v")) u_code (
    .addr(pc), .data({csr_addr, u_code_data}));
  csr #(.applicationType("IVERILOG"), .CodeFile("C:\\Users\\kevin\\Desktop\\Single-cycle-RISCV\\user\\src\\csr.v")) u_csr (
    .clk(clk), .rstn(in_2), .we(csr), .addr(csr_addr), .din(u_csr_op_c), .exception(exception),
    .cause(cause), .pc(pc), .uret(uret), .interrupt(interrupt), .icause(32'h80000008), .pc4(pc_plus_4),
    .dout(csrReadData), .trap(trap), .utvec(utvec), .uepc(epc));
  Registers #(.applicationType("IVERILOG"), .CodeFile("C:\\Users\\kevin\\Desktop\\Single-cycle-RISCV\\user\\src\\Registers.v")) u_Registers (
    .clk(clk), .we(wreg), .rs1(rs1), .rs2(rs2), .rd(rd), .din(multiplexer_4_out), .r1(r1), .r2(memWriteData));
  // Probe on {csr_addr, u_code_data}
  // Probe on r1
  // Probe on memWriteData
  Decode #(.applicationType("IVERILOG"), .CodeFile("C:\\Users\\kevin\\Desktop\\Single-cycle-RISCV\\user\\src\\Decode.v")) u_Decode (
    .instr({csr_addr, u_code_data}), .rs1(rs1), .rs2(rs2), .rd(rd), .Imm(Imm), .wreg(wreg),
    .wregSrc(wregSrc), .pcSrc(pcSrc), .jalr(jalr), .btype(btype), .funct3(funct3), .ALU_op(ALU_op),
    .aluSrcB(aluSrcB), .store(store), .load(load), .csr(csr), .exception(exception), .cause(cause),
    .uret(uret));
  Multiplexer #(.Bits(32)) multiplexer_3 (.sel(jalr), .in_0(pc), .in_1(r1), .out(multiplexer_3_out));
  csr_op #(.applicationType("IVERILOG"), .CodeFile("C:\\Users\\kevin\\Desktop\\Single-cycle-RISCV\\user\\src\\csr_op.v")) u_csr_op (
    .funct3(funct3), .a(csrReadData), .r1(r1), .imm(rs1), .c(u_csr_op_c));
  add #(.applicationType("IVERILOG"), .CodeFile("C:\\Users\\kevin\\Desktop\\Single-cycle-RISCV\\user\\src\\add.v")) u_add (
    .a(Imm), .b(multiplexer_3_out), .c(jal_jalr));
  // Probe on multiplexer_4_out
  Multiplexer #(.Selector_Bits(2), .Bits(32)) multiplexer_4 (
    .sel(wregSrc), .in_0(Imm), .in_1(jal_jalr), .in_2(pc_plus_4), .in_3(dout), .out(multiplexer_4_out));
  // Probe on rs1
  // Probe on rs2
  // Probe on rd
  // Probe on Imm
  // Probe on wreg
  // Probe on wregSrc
  // Probe on pcSrc
  // Probe on jalr
  // Probe on btype
  // Probe on funct3
  // Probe on ALU_op
  // Probe on aluSrcB
  // Probe on store
  // Probe on load
  Multiplexer #(.Bits(32)) multiplexer_5 (.sel(aluSrcB), .in_0(memWriteData), .in_1(Imm), .out(multiplexer_5_out));
  // Probe on multiplexer_5_out
  branch #(.applicationType("IVERILOG"), .CodeFile("C:\\Users\\kevin\\Desktop\\Single-cycle-RISCV\\user\\src\\branch.v")) u_branch (
    .funct3(funct3), .r1(r1), .r2(memWriteData), .branch(branch));
  // Probe on r1
  ALU #(.applicationType("IVERILOG"), .CodeFile("C:\\Users\\kevin\\Desktop\\Single-cycle-RISCV\\user\\src\\ALU.v")) u_ALU (
    .a(r1), .b(multiplexer_5_out), .ALU_op(ALU_op), .c(c));
  // Probe on c
  // Probe on memReadData
  // Probe on memWriteData
  // Probe on store
  DipSwitch dipswitch_1 (.out(dipswitch_1_out));
  DipSwitch dipswitch_2 (.out(dipswitch_2_out));
  DipSwitch dipswitch_3 (.out(dipswitch_3_out));
  DipSwitch dipswitch_4 (.out(dipswitch_4_out));
  DipSwitch dipswitch_5 (.out(dipswitch_5_out));
  DipSwitch dipswitch_6 (.out(dipswitch_6_out));
  DipSwitch dipswitch_7 (.out(dipswitch_7_out));
  DipSwitch dipswitch_8 (.out(dipswitch_8_out));
  Keyboard keyboard_1 (.C(clk), .en(u_term_key_en), .D(keyboard_1_d), .av(keyboard_1_av));
  Data #(.applicationType("IVERILOG"), .CodeFile("C:\\Users\\kevin\\Desktop\\Single-cycle-RISCV\\user\\src\\Data.v")) u_Data (
    .clk(clk), .we(store), .funct3(funct3), .addr(c), .din(memWriteData), .dout(memReadData));
  timer #(.applicationType("IVERILOG"), .CodeFile("C:\\Users\\kevin\\Desktop\\Single-cycle-RISCV\\user\\src\\timer.v")) u_timer (
    .clk(clk), .rstn(in_2), .we(store), .addr(c), .din(memWriteData), .dout(memReadData));
  led #(.applicationType("IVERILOG"), .CodeFile("C:\\Users\\kevin\\Desktop\\Single-cycle-RISCV\\user\\src\\led.v")) u_led (
    .clk(clk), .rstn(in_2), .we(store), .addr(c), .din(memWriteData), .led(u_led_led));
  button #(.applicationType("IVERILOG"), .CodeFile("C:\\Users\\kevin\\Desktop\\Single-cycle-RISCV\\user\\src\\button.v")) u_button (
    .clk(clk), .rstn(in_2), .we(store), .addr(c), .din(memWriteData), .b0(dipswitch_1_out),
    .b1(dipswitch_2_out), .b2(dipswitch_3_out), .b3(dipswitch_4_out), .b4(dipswitch_5_out),
    .b5(dipswitch_6_out), .b6(dipswitch_7_out), .b7(dipswitch_8_out), .dout(memReadData),
    .interrupt(interrupt));
  disp #(.applicationType("IVERILOG"), .CodeFile("C:\\Users\\kevin\\Desktop\\Single-cycle-RISCV\\user\\src\\disp.v")) u_disp (
    .clk(clk), .rstn(in_2), .we(store), .addr(c), .din(memWriteData), .vaddr(u_disp_vaddr),
    .vdata(u_disp_vdata), .vwe(u_disp_vwe));
  term #(.applicationType("IVERILOG"), .CodeFile("C:\\Users\\kevin\\Desktop\\Single-cycle-RISCV\\user\\src\\term.v")) u_term (
    .clk(clk), .rstn(in_2), .we(store), .addr(c), .din(memWriteData), .key_data(keyboard_1_d),
    .key_av(keyboard_1_av), .dout(memReadData), .key_en(u_term_key_en), .term_data(u_term_term_data),
    .term_en(u_term_term_en));
  GraphicCard #(.graphicHeight(128), .graphicWidth(128), .Bits(8)) graphiccard_1 (
    .A(u_disp_vaddr), .str(u_disp_vwe), .C(clk), .ld(1'b0), .B(1'b0), .D(u_disp_vdata));
  Multiplexer #(.Bits(32)) multiplexer_6 (.sel(load), .in_0(c), .in_1(memReadData), .out(multiplexer_6_out));
  LED led_2 (.in(u_led_led[0]));
  LED led_3 (.in(u_led_led[1]));
  LED led_4 (.in(u_led_led[2]));
  LED led_5 (.in(u_led_led[3]));
  LED led_6 (.in(u_led_led[4]));
  LED led_7 (.in(u_led_led[5]));
  LED led_8 (.in(u_led_led[6]));
  LED led_9 (.in(u_led_led[7]));
  Terminal terminal_1 (.D(u_term_term_data), .C(clk), .en(u_term_term_en));
  Multiplexer #(.Bits(32)) multiplexer_7 (.sel(csr), .in_0(multiplexer_6_out), .in_1(csrReadData), .out(dout));

  // Other names for the same wires on the sheet: memAddr[31:0] = c; r2[31:0] = memWriteData; rstn = in_2;
  //   wmem = store

  // Notes on the sheet:
  //   clk: Hz: 100
  //   lui
  //   auipc
endmodule
